# Fritzing sketch 8377169abcd4455c9a227b257d124988 (saved by Fritzing 0.9.3b)
breadboards: 1

parts:
  IC1 = PICAXE-18 [package=THT]
  LED1 = LED - 5mm [color="Orange (620nm)" package="5 mm [THT]"]
  LED2 = LED - 5mm [color="Orange (620nm)" package="5 mm [THT]"]
  LED3 = LED - 5mm [color="Orange (620nm)" package="5 mm [THT]"]
  S1 = Pushbutton [package="[THT]"]
  R1 = Resistor [tolerance=±5% resistance=720 package=THT]
  R2 = Resistor [tolerance=±5% resistance=720 package=THT]
  R3 = Resistor [tolerance=±5% resistance=720 package=THT]
  R4 = Resistor [tolerance=±5% resistance=10k package=THT]
  LED4 = LED - 5mm [color="Green (555nm)" package="5 mm [THT]"]
  LED5 = LED - 5mm [color="Green (555nm)" package="5 mm [THT]"]
  LED6 = LED - 5mm [color="Green (555nm)" package="5 mm [THT]"]
  LED7 = LED - 5mm [color="Green (555nm)" package="5 mm [THT]"]
  LED8 = LED - 5mm [color="Green (555nm)" package="5 mm [THT]"]
  LED9 = LED - 5mm [color="Green (555nm)" package="5 mm [THT]"]
  LED10 = LED - 5mm [color="Green (555nm)" package="5 mm [THT]"]
  LED11 = LED - 5mm [color="Green (555nm)" package="5 mm [THT]"]
  VCC2 = Battery block 9V

nets:
  N1: IC1.Serial_Out, LED1.cathode
  N2: IC1.0V, IC1.In_0, S1.Pin_1, S1.Pin_2, S1.Pin_3, S1.Pin_4, R2.Pin_1, R3.Pin_1, VCC2.-
  N3: IC1.Out_0, LED4.anode
  N4: IC1.Out_1, LED5.anode
  N5: IC1.Out_2, LED6.anode
  N6: IC1.Out_3, LED7.anode
  N7: IC1.Out_5, LED9.anode
  N8: IC1.Out_6, LED10.anode
  N9: IC1.Out_7, LED11.anode
  N10: IC1.+V, R1.Pin_0, R3.Pin_0, VCC2.+
  N11: IC1.In_6, LED2.cathode
  N12: IC1.In_7, LED3.cathode
  N13: IC1.In_1, R4.Pin_1
  N14: LED1.anode, LED2.anode, LED3.anode, R1.Pin_1, R4.Pin_0
  N15: R2.Pin_0, LED4.cathode, LED5.cathode, LED6.cathode, LED7.cathode, LED8.cathode, LED9.cathode, LED10.cathode, LED11.cathode

notes:
  10k
  720
